// Logisim project main.circ as structural Verilog: 1 circuit, main circuit main
module main (
);

  wire and_1_out, and_2_out, and_3_out, and_4_out, and_5_out, and_6_out, cdm_8_1_p3, cl, code,
       comparator_1_eq, comparator_2_eq, comparator_3_eq, comparator_4_eq, comparator_4_gt, comparator_5_eq,
       comparator_6_eq, data, display_driver_rev2_2_cl_2, display_driver_rev2_2_r_w_2,
       display_driver_rev2_3_cl_2, display_driver_rev2_3_r_w_2, display_driver_rev2_4_cl_2,
       display_driver_rev2_4_r_w_2, display_driver_rev2_5_cl_2, display_driver_rev2_5_r_w_2,
       display_driver_rev2_6_cl_2, display_driver_rev2_6_r_w_2, display_driver_rev2_7_cl_2,
       display_driver_rev2_7_r_w_2, display_driver_rev2_8_cl_2, display_driver_rev2_8_r_w_2,
       display_driver_rev2_9_cl_2, display_driver_rev2_9_r_w_2, display_driver_rev2_10_cl_2,
       display_driver_rev2_10_r_w_2, display_driver_rev2_11_cl_2, display_driver_rev2_11_r_w_2,
       display_driver_rev2_12_cl_2, display_driver_rev2_12_r_w_2, display_driver_rev2_13_cl_2,
       display_driver_rev2_13_r_w_2, display_driver_rev2_14_cl_2, display_driver_rev2_14_r_w_2, ext_sriver,
       mem, not_1_out, not_2_out, r_w, reset, w_r_driver;
  wire [3:0] display_driver_rev2_1_bcd_1, display_driver_rev2_1_bcd_2, display_driver_rev2_2_addr_out,
       display_driver_rev2_2_addr_out_chain, display_driver_rev2_2_bcd_1, display_driver_rev2_2_bcd_2,
       display_driver_rev2_3_addr_out, display_driver_rev2_3_addr_out_chain, display_driver_rev2_3_bcd_1,
       display_driver_rev2_3_bcd_2, display_driver_rev2_4_addr_out, display_driver_rev2_4_addr_out_chain,
       display_driver_rev2_4_bcd_1, display_driver_rev2_4_bcd_2, display_driver_rev2_5_addr_out,
       display_driver_rev2_5_addr_out_chain, display_driver_rev2_5_bcd_1, display_driver_rev2_5_bcd_2,
       display_driver_rev2_6_addr_out, display_driver_rev2_6_addr_out_chain, display_driver_rev2_6_bcd_1,
       display_driver_rev2_6_bcd_2, display_driver_rev2_7_addr_out, display_driver_rev2_7_addr_out_chain,
       display_driver_rev2_7_bcd_1, display_driver_rev2_7_bcd_2, display_driver_rev2_8_addr_out,
       display_driver_rev2_8_addr_out_chain, display_driver_rev2_8_bcd_1, display_driver_rev2_8_bcd_2,
       display_driver_rev2_9_addr_out, display_driver_rev2_9_addr_out_chain, display_driver_rev2_9_bcd_1,
       display_driver_rev2_9_bcd_2, display_driver_rev2_10_addr_out, display_driver_rev2_10_addr_out_chain,
       display_driver_rev2_10_bcd_1, display_driver_rev2_10_bcd_2, display_driver_rev2_11_addr_out,
       display_driver_rev2_11_addr_out_chain, display_driver_rev2_11_bcd_1, display_driver_rev2_11_bcd_2,
       display_driver_rev2_12_addr_out, display_driver_rev2_12_addr_out_chain, display_driver_rev2_12_bcd_1,
       display_driver_rev2_12_bcd_2, display_driver_rev2_13_addr_out, display_driver_rev2_13_addr_out_chain,
       display_driver_rev2_13_bcd_1, display_driver_rev2_13_bcd_2, display_driver_rev2_14_addr_out,
       display_driver_rev2_14_addr_out_chain, display_driver_rev2_14_bcd_1, display_driver_rev2_14_bcd_2,
       driver_add, incrementer_1_out_2;
  wire [7:0] addr, bank_n, cdm_8_1_p7, cdm_8_1_p8, data_write, display_driver_rev2_2_data_out,
       display_driver_rev2_3_data_out, display_driver_rev2_4_data_out, display_driver_rev2_5_data_out,
       display_driver_rev2_6_data_out, display_driver_rev2_7_data_out, display_driver_rev2_8_data_out,
       display_driver_rev2_9_data_out, display_driver_rev2_10_data_out, display_driver_rev2_11_data_out,
       display_driver_rev2_12_data_out, display_driver_rev2_13_data_out, display_driver_rev2_14_data_out, IO;
  wire [7:5] register_3_q;

  Clock clock_1 (.out(cl));
  Button button_1 (.out(reset));
  Comparator comparator_1 (.a(addr), .b({8{1'b1}}), .eq(comparator_1_eq));  // open: gt, lt
  and and_1 (and_1_out, comparator_1_eq, data);
  Comparator comparator_2 (.a(addr), .b(8'hfe), .eq(comparator_2_eq));  // open: gt, lt
  and and_2 (and_2_out, comparator_2_eq, data);
  Comparator comparator_3 (.a(addr), .b(8'hfc), .eq(comparator_3_eq));  // open: gt, lt
  and and_3 (and_3_out, comparator_3_eq, data);
  Comparator #(.mode("unsigned")) comparator_4 (
    .a(addr), .b(8'hfb), .gt(comparator_4_gt), .eq(comparator_4_eq));  // open: lt
  Register register_1 (.D(IO), .en(and_1_out), .Q(bank_n), .clk(cl), .clr(reset));
  Register register_2 (.D(IO), .en(and_2_out), .Q(data_write), .clk(cl), .clr(reset));
  Register register_3 (.D(IO), .en(and_3_out), .Q({register_3_q, w_r_driver, driver_add}), .clk(cl), .clr(reset));
  or or_1 (ext_sriver, comparator_4_gt, comparator_4_eq);
  Decoder #(.disabled(0)) decoder_1 (.out0(code), .out1(data), .sel(cdm_8_1_p3), .en(mem));
  // CdM_8 cdm_8_1: pin names not known; wires that end beside it: cl, reset, cdm_8_1_p3, mem, r_w, addr, cdm_8_1_p7, cdm_8_1_p8
  assign IO = not_1_out ? cdm_8_1_p7 : 8'bz;  // Controlled_Buffer controlled_buffer_1
  not not_1 (not_1_out, r_w);
  assign cdm_8_1_p8 = r_w ? IO : 8'bz;  // Controlled_Buffer controlled_buffer_2
  and and_4 (and_4_out, not_2_out, data);
  not not_2 (not_2_out, ext_sriver);
  and and_5 (and_5_out, code, comparator_5_eq);
  Comparator comparator_5 (.a(bank_n), .b({8{1'b0}}), .eq(comparator_5_eq));  // open: gt, lt
  and and_6 (and_6_out, code, comparator_6_eq);
  Comparator comparator_6 (.a(bank_n), .b(8'h1), .eq(comparator_6_eq));  // open: gt, lt
  RAM ram_1 (.addr(addr), .data(IO), .sel(and_4_out), .clk(cl), .ld(r_w), .clr(reset));
  ROM rom_1 (.addr(addr), .data(IO), .sel(and_5_out));
  ROM rom_2 (.addr(addr), .data(IO), .sel(and_6_out));
  display_driver_rev2 display_driver_rev2_1 (
    .addr_in(display_driver_rev2_2_addr_out), .addr_in_chain(display_driver_rev2_2_addr_out_chain),
    .data(display_driver_rev2_2_data_out), .cl(display_driver_rev2_2_cl_2),
    .bcd_1(display_driver_rev2_1_bcd_1), .bcd_2(display_driver_rev2_1_bcd_2),
    .r_w(display_driver_rev2_2_r_w_2));  // open: addr_out, addr_out_chain, data_out, cl_2, is_0, r_w_2
  Hex_Digit_Display hex_digit_display_1 (.value(display_driver_rev2_1_bcd_2));  // open: dp
  Hex_Digit_Display hex_digit_display_2 (.value(display_driver_rev2_1_bcd_1));  // open: dp
  display_driver_rev2 display_driver_rev2_2 (
    .addr_in(display_driver_rev2_3_addr_out), .addr_in_chain(display_driver_rev2_3_addr_out_chain),
    .data(display_driver_rev2_3_data_out), .cl(display_driver_rev2_3_cl_2),
    .addr_out(display_driver_rev2_2_addr_out), .addr_out_chain(display_driver_rev2_2_addr_out_chain),
    .data_out(display_driver_rev2_2_data_out), .cl_2(display_driver_rev2_2_cl_2),
    .bcd_1(display_driver_rev2_2_bcd_1), .bcd_2(display_driver_rev2_2_bcd_2),
    .r_w(display_driver_rev2_3_r_w_2), .r_w_2(display_driver_rev2_2_r_w_2));  // open: is_0
  Hex_Digit_Display hex_digit_display_3 (.value(display_driver_rev2_2_bcd_1));  // open: dp
  Hex_Digit_Display hex_digit_display_4 (.value(display_driver_rev2_4_bcd_1));  // open: dp
  display_driver_rev2 display_driver_rev2_3 (
    .addr_in(display_driver_rev2_5_addr_out), .addr_in_chain(display_driver_rev2_5_addr_out_chain),
    .data(display_driver_rev2_5_data_out), .cl(display_driver_rev2_5_cl_2),
    .addr_out(display_driver_rev2_3_addr_out), .addr_out_chain(display_driver_rev2_3_addr_out_chain),
    .data_out(display_driver_rev2_3_data_out), .cl_2(display_driver_rev2_3_cl_2),
    .bcd_1(display_driver_rev2_3_bcd_1), .bcd_2(display_driver_rev2_3_bcd_2),
    .r_w(display_driver_rev2_5_r_w_2), .r_w_2(display_driver_rev2_3_r_w_2));  // open: is_0
  Hex_Digit_Display hex_digit_display_5 (.value(display_driver_rev2_2_bcd_2));  // open: dp
  Hex_Digit_Display hex_digit_display_6 (.value(display_driver_rev2_4_bcd_2));  // open: dp
  Hex_Digit_Display hex_digit_display_7 (.value(display_driver_rev2_3_bcd_2));  // open: dp
  Hex_Digit_Display hex_digit_display_8 (.value(display_driver_rev2_3_bcd_1));  // open: dp
  Hex_Digit_Display hex_digit_display_9 (.value(display_driver_rev2_6_bcd_1));  // open: dp
  Hex_Digit_Display hex_digit_display_10 (.value(display_driver_rev2_6_bcd_2));  // open: dp
  display_driver_rev2 display_driver_rev2_4 (
    .addr_in_chain(4'b0000), .addr_out(display_driver_rev2_4_addr_out),
    .addr_out_chain(display_driver_rev2_4_addr_out_chain), .data_out(display_driver_rev2_4_data_out),
    .cl_2(display_driver_rev2_4_cl_2), .bcd_1(display_driver_rev2_4_bcd_1),
    .bcd_2(display_driver_rev2_4_bcd_2), .r_w_2(display_driver_rev2_4_r_w_2));  // open: addr_in, data, cl, is_0, r_w
  display_driver_rev2 display_driver_rev2_5 (
    .addr_in(display_driver_rev2_7_addr_out), .addr_in_chain(display_driver_rev2_7_addr_out_chain),
    .data(display_driver_rev2_7_data_out), .cl(display_driver_rev2_7_cl_2),
    .addr_out(display_driver_rev2_5_addr_out), .addr_out_chain(display_driver_rev2_5_addr_out_chain),
    .data_out(display_driver_rev2_5_data_out), .cl_2(display_driver_rev2_5_cl_2),
    .bcd_1(display_driver_rev2_5_bcd_1), .bcd_2(display_driver_rev2_5_bcd_2),
    .r_w(display_driver_rev2_7_r_w_2), .r_w_2(display_driver_rev2_5_r_w_2));  // open: is_0
  Hex_Digit_Display hex_digit_display_11 (.value(display_driver_rev2_5_bcd_1));  // open: dp
  Hex_Digit_Display hex_digit_display_12 (.value(display_driver_rev2_8_bcd_1));  // open: dp
  display_driver_rev2 display_driver_rev2_6 (
    .addr_in(display_driver_rev2_4_addr_out), .addr_in_chain(display_driver_rev2_4_addr_out_chain),
    .data(display_driver_rev2_4_data_out), .cl(display_driver_rev2_4_cl_2),
    .addr_out(display_driver_rev2_6_addr_out), .addr_out_chain(display_driver_rev2_6_addr_out_chain),
    .data_out(display_driver_rev2_6_data_out), .cl_2(display_driver_rev2_6_cl_2),
    .bcd_1(display_driver_rev2_6_bcd_1), .bcd_2(display_driver_rev2_6_bcd_2),
    .r_w(display_driver_rev2_4_r_w_2), .r_w_2(display_driver_rev2_6_r_w_2));  // open: is_0
  display_driver_rev2 display_driver_rev2_7 (
    .addr_in(display_driver_rev2_9_addr_out), .addr_in_chain(display_driver_rev2_9_addr_out_chain),
    .data(display_driver_rev2_9_data_out), .cl(display_driver_rev2_9_cl_2),
    .addr_out(display_driver_rev2_7_addr_out), .addr_out_chain(display_driver_rev2_7_addr_out_chain),
    .data_out(display_driver_rev2_7_data_out), .cl_2(display_driver_rev2_7_cl_2),
    .bcd_1(display_driver_rev2_7_bcd_1), .bcd_2(display_driver_rev2_7_bcd_2),
    .r_w(display_driver_rev2_9_r_w_2), .r_w_2(display_driver_rev2_7_r_w_2));  // open: is_0
  Hex_Digit_Display hex_digit_display_13 (.value(display_driver_rev2_5_bcd_2));  // open: dp
  Hex_Digit_Display hex_digit_display_14 (.value(display_driver_rev2_8_bcd_2));  // open: dp
  Hex_Digit_Display hex_digit_display_15 (.value(display_driver_rev2_7_bcd_2));  // open: dp
  Hex_Digit_Display hex_digit_display_16 (.value(display_driver_rev2_7_bcd_1));  // open: dp
  Hex_Digit_Display hex_digit_display_17 (.value(display_driver_rev2_10_bcd_2));  // open: dp
  Hex_Digit_Display hex_digit_display_18 (.value(display_driver_rev2_10_bcd_1));  // open: dp
  display_driver_rev2 display_driver_rev2_8 (
    .addr_in(display_driver_rev2_6_addr_out), .addr_in_chain(display_driver_rev2_6_addr_out_chain),
    .data(display_driver_rev2_6_data_out), .cl(display_driver_rev2_6_cl_2),
    .addr_out(display_driver_rev2_8_addr_out), .addr_out_chain(display_driver_rev2_8_addr_out_chain),
    .data_out(display_driver_rev2_8_data_out), .cl_2(display_driver_rev2_8_cl_2),
    .bcd_1(display_driver_rev2_8_bcd_1), .bcd_2(display_driver_rev2_8_bcd_2),
    .r_w(display_driver_rev2_6_r_w_2), .r_w_2(display_driver_rev2_8_r_w_2));  // open: is_0
  display_driver_rev2 display_driver_rev2_9 (
    .addr_in(display_driver_rev2_11_addr_out), .addr_in_chain(display_driver_rev2_11_addr_out_chain),
    .data(display_driver_rev2_11_data_out), .cl(display_driver_rev2_11_cl_2),
    .addr_out(display_driver_rev2_9_addr_out), .addr_out_chain(display_driver_rev2_9_addr_out_chain),
    .data_out(display_driver_rev2_9_data_out), .cl_2(display_driver_rev2_9_cl_2),
    .bcd_1(display_driver_rev2_9_bcd_1), .bcd_2(display_driver_rev2_9_bcd_2),
    .r_w(display_driver_rev2_11_r_w_2), .r_w_2(display_driver_rev2_9_r_w_2));  // open: is_0
  Hex_Digit_Display hex_digit_display_19 (.value(display_driver_rev2_9_bcd_1));  // open: dp
  Hex_Digit_Display hex_digit_display_20 (.value(display_driver_rev2_12_bcd_1));  // open: dp
  display_driver_rev2 display_driver_rev2_10 (
    .addr_in(display_driver_rev2_8_addr_out), .addr_in_chain(display_driver_rev2_8_addr_out_chain),
    .data(display_driver_rev2_8_data_out), .cl(display_driver_rev2_8_cl_2),
    .addr_out(display_driver_rev2_10_addr_out), .addr_out_chain(display_driver_rev2_10_addr_out_chain),
    .data_out(display_driver_rev2_10_data_out), .cl_2(display_driver_rev2_10_cl_2),
    .bcd_1(display_driver_rev2_10_bcd_1), .bcd_2(display_driver_rev2_10_bcd_2),
    .r_w(display_driver_rev2_8_r_w_2), .r_w_2(display_driver_rev2_10_r_w_2));  // open: is_0
  display_driver_rev2 display_driver_rev2_11 (
    .addr_in(display_driver_rev2_14_addr_out), .addr_in_chain(incrementer_1_out_2),
    .data(display_driver_rev2_14_data_out), .cl(display_driver_rev2_14_cl_2),
    .addr_out(display_driver_rev2_11_addr_out), .addr_out_chain(display_driver_rev2_11_addr_out_chain),
    .data_out(display_driver_rev2_11_data_out), .cl_2(display_driver_rev2_11_cl_2),
    .bcd_1(display_driver_rev2_11_bcd_1), .bcd_2(display_driver_rev2_11_bcd_2),
    .r_w(display_driver_rev2_14_r_w_2), .r_w_2(display_driver_rev2_11_r_w_2));  // open: is_0
  Hex_Digit_Display hex_digit_display_21 (.value(display_driver_rev2_9_bcd_2));  // open: dp
  Hex_Digit_Display hex_digit_display_22 (.value(display_driver_rev2_12_bcd_2));  // open: dp
  Hex_Digit_Display hex_digit_display_23 (.value(display_driver_rev2_11_bcd_1));  // open: dp
  Hex_Digit_Display hex_digit_display_24 (.value(display_driver_rev2_11_bcd_2));  // open: dp
  Hex_Digit_Display hex_digit_display_25 (.value(display_driver_rev2_13_bcd_1));  // open: dp
  Hex_Digit_Display hex_digit_display_26 (.value(display_driver_rev2_13_bcd_2));  // open: dp
  display_driver_rev2 display_driver_rev2_12 (
    .addr_in(display_driver_rev2_10_addr_out), .addr_in_chain(display_driver_rev2_10_addr_out_chain),
    .data(display_driver_rev2_10_data_out), .cl(display_driver_rev2_10_cl_2),
    .addr_out(display_driver_rev2_12_addr_out), .addr_out_chain(display_driver_rev2_12_addr_out_chain),
    .data_out(display_driver_rev2_12_data_out), .cl_2(display_driver_rev2_12_cl_2),
    .bcd_1(display_driver_rev2_12_bcd_1), .bcd_2(display_driver_rev2_12_bcd_2),
    .r_w(display_driver_rev2_10_r_w_2), .r_w_2(display_driver_rev2_12_r_w_2));  // open: is_0
  display_driver_rev2 display_driver_rev2_13 (
    .addr_in(display_driver_rev2_12_addr_out), .addr_in_chain(display_driver_rev2_12_addr_out_chain),
    .data(display_driver_rev2_12_data_out), .cl(display_driver_rev2_12_cl_2),
    .addr_out(display_driver_rev2_13_addr_out), .addr_out_chain(display_driver_rev2_13_addr_out_chain),
    .data_out(display_driver_rev2_13_data_out), .cl_2(display_driver_rev2_13_cl_2),
    .bcd_1(display_driver_rev2_13_bcd_1), .bcd_2(display_driver_rev2_13_bcd_2),
    .r_w(display_driver_rev2_12_r_w_2), .r_w_2(display_driver_rev2_13_r_w_2));  // open: is_0
  incrementer incrementer_1 (.in_1(display_driver_rev2_14_addr_out_chain), .out_2(incrementer_1_out_2));
  Hex_Digit_Display hex_digit_display_27 (.value(display_driver_rev2_14_bcd_1));  // open: dp
  Hex_Digit_Display hex_digit_display_28 (.value(display_driver_rev2_14_bcd_2));  // open: dp
  display_driver_rev2 display_driver_rev2_14 (
    .addr_in(display_driver_rev2_13_addr_out), .addr_in_chain(display_driver_rev2_13_addr_out_chain),
    .data(display_driver_rev2_13_data_out), .cl(display_driver_rev2_13_cl_2),
    .addr_out(display_driver_rev2_14_addr_out), .addr_out_chain(display_driver_rev2_14_addr_out_chain),
    .data_out(display_driver_rev2_14_data_out), .cl_2(display_driver_rev2_14_cl_2),
    .bcd_1(display_driver_rev2_14_bcd_1), .bcd_2(display_driver_rev2_14_bcd_2),
    .r_w(display_driver_rev2_13_r_w_2), .r_w_2(display_driver_rev2_14_r_w_2));  // open: is_0

  // Notes on the sheet:
  //   contents of rom_1 (hex, n*v repeats v):
  //   d1 f0 cc f0 d1 d d2 0 d3 4 5 e4 12 ab 8e 89 ee a d0 0 d1 6 a4 d1 d a4 d0 1 d1 10 d2 6 a e4 29 a4 8a
  //   8c 8d ee 20 8c d2 6 a e4 35 a4 8a 8c 8d ee 2c ee f7 192*0 d1 ff d0 1 a4 ee 0 d4
  //   contents of rom_2 (hex, n*v repeats v):
  //   d1 f0 cc f0 d1 d d2 0 d3 4 5 e4 12 ab 8e 89 ee a d0 0 d1 6 a4 d1 d a4 d0 1 d1 10 d2 6 a e4 29 a4 8a
  //   8c 8d ee 20 8c d2 6 a e4 35 a4 8a 8c 8d ee 2c ee f7 192*0 d1 ff d0 1 a4 ee 0 d4
endmodule
